# Fritzing sketch arduinoMinCkt (saved by Fritzing 0.8.5b)
circuit board: 8.46667cm x 5.64444cm
breadboards: 1

parts:
  U1 = Voltage Regulator - 5V [package="DPak [SMD]"]
  C1 = Electrolytic Capacitor [capacitance=10µF package="0405 [SMD, electrolytic]"]
  C2 = Electrolytic Capacitor [capacitance=100µF package="0405 [SMD, electrolytic]"]
  D1 = Rectifier Diode [part_number=1N4001 package="300 mil [THT]"]
  Power_plug1 = Power plug
  U2 = atmega328 [package=dip]
  XTAL1 = Crystal [frequency="16 Mhz" package=SMD]
  C3 = Ceramic Capacitor [capacitance=1pF package="1206 [SMD, multilayer]"]
  C4 = Ceramic Capacitor [capacitance=1pF package="1206 [SMD, multilayer]"]
  R1 = Resistor [tolerance=±5% resistance=10k package=THT]
  S1 = Pushbutton [package="[THT]"]

nets:
  N1: U1.input_voltage, C2.+, D1.cathode
  GND: U1.GND, C1.-, C2.-, Power_plug1.GND, U2.GND, C3.0, C4.1, S1.Pin_3, S1.Pin_4
  N2: U1.output_voltage, C1.+, U2.VCC, U2.AVCC, U2.AREF, R1.Pin_1
  N3: D1.anode, Power_plug1.VCC
  N4: U2.RESET, R1.Pin_0, S1.Pin_1, S1.Pin_2
  N5: U2.XLAT1, XTAL1.pin_0, C3.1
  N6: U2.XLAT2, XTAL1.pin_1, C4.0
